// Digital circuit Multiplexador_8bit.dig as structural Verilog
module Multiplexador_8bit (
  input  [7:0] A,
  input  [7:0] B,
  input  [7:0] C,
  input  [7:0] D,
  input  [7:0] E,
  input  [7:0] F,
  input  [7:0] G,
  input  [7:0] H,
  input  [7:0] SELECT_1,
  input  [7:0] SELECT_2,
  input  [7:0] SELECT_3,
  output [7:0] S
);

  wire [7:0] and_1_out, and_2_out, and_3_out, and_4_out, and_5_out, and_6_out, and_7_out, and_8_out,
       not_1_out, not_2_out, not_3_out, not_4_out, not_5_out, not_6_out, not_7_out, not_8_out, not_9_out,
       not_10_out, not_11_out, not_12_out, or_1_out, or_2_out;

  assign not_1_out = ~SELECT_1;  // Not not_1, 8 bits wide
  assign not_2_out = ~SELECT_2;  // Not not_2, 8 bits wide
  assign not_3_out = ~SELECT_3;  // Not not_3, 8 bits wide
  assign not_4_out = ~SELECT_1;  // Not not_4, 8 bits wide
  assign not_5_out = ~SELECT_3;  // Not not_5, 8 bits wide
  assign not_6_out = ~SELECT_1;  // Not not_6, 8 bits wide
  assign not_7_out = ~SELECT_2;  // Not not_7, 8 bits wide
  assign not_8_out = ~SELECT_2;  // Not not_8, 8 bits wide
  assign not_9_out = ~SELECT_3;  // Not not_9, 8 bits wide
  assign not_10_out = ~SELECT_1;  // Not not_10, 8 bits wide
  assign not_11_out = ~SELECT_2;  // Not not_11, 8 bits wide
  assign not_12_out = ~SELECT_3;  // Not not_12, 8 bits wide
  assign and_1_out = A & not_1_out & not_2_out & not_3_out;  // And and_1, 8 bits wide
  assign and_2_out = B & not_4_out & SELECT_2 & not_5_out;  // And and_2, 8 bits wide
  assign and_3_out = C & not_6_out & not_7_out & SELECT_3;  // And and_3, 8 bits wide
  assign and_4_out = D & SELECT_1 & not_8_out & not_9_out;  // And and_4, 8 bits wide
  assign and_5_out = E & not_10_out & SELECT_2 & SELECT_3;  // And and_5, 8 bits wide
  assign and_6_out = F & SELECT_1 & not_11_out & SELECT_3;  // And and_6, 8 bits wide
  assign and_7_out = G & SELECT_1 & SELECT_2 & not_12_out;  // And and_7, 8 bits wide
  assign and_8_out = H & SELECT_1 & SELECT_2 & SELECT_3;  // And and_8, 8 bits wide
  assign or_1_out = and_1_out | and_2_out | and_3_out | and_4_out;  // Or or_1, 8 bits wide
  assign or_2_out = and_5_out | and_6_out | and_7_out | and_8_out;  // Or or_2, 8 bits wide
  assign S = or_1_out | or_2_out;  // Or or_3, 8 bits wide
endmodule
