// Digital circuit Multiplicacao_8bit-Errado.dig as structural Verilog
module Multiplicacao_8bit_Errado (
  input  [3:0] A,
  input  [3:0] B,
  output [15:0] out_3
);

  wire and_2_out, and_3_out, and_4_out, and_5_out, and_6_out, and_7_out, and_8_out, and_9_out, and_10_out,
       and_11_out, and_12_out, and_13_out, and_14_out, and_15_out, and_16_out, soma_1bit_1_cout,
       soma_1bit_2_cout, soma_1bit_3_cout, soma_1bit_4_cout, soma_1bit_5_cout, soma_1bit_6_cout,
       soma_1bit_7_cout, soma_1bit_8_cout, soma_1bit_9_cout, soma_1bit_10_cout, soma_1bit_11_cout,
       soma_1bit_12_cout, soma_1bit_13_cout;

  and and_1 (out_3[0], A[0], B[0]);
  and and_2 (and_2_out, A[0], B[1]);
  and and_3 (and_3_out, A[0], B[2]);
  and and_4 (and_4_out, A[0], B[3]);
  and and_5 (and_5_out, A[1], B[0]);
  and and_6 (and_6_out, A[1], B[1]);
  and and_7 (and_7_out, A[1], B[2]);
  and and_8 (and_8_out, A[1], B[3]);
  and and_9 (and_9_out, A[2], B[0]);
  and and_10 (and_10_out, A[2], B[1]);
  and and_11 (and_11_out, A[2], B[2]);
  and and_12 (and_12_out, A[2], B[3]);
  and and_13 (and_13_out, A[3], B[0]);
  and and_14 (and_14_out, A[3], B[1]);
  and and_15 (and_15_out, A[3], B[2]);
  and and_16 (and_16_out, A[3], B[3]);
  Soma_1bit soma_1bit_1 (.A(and_2_out), .B(and_3_out), .Cin(1'b0), .S(out_3[1]), .Cout(soma_1bit_1_cout));
  Soma_1bit soma_1bit_2 (.A(soma_1bit_1_cout), .B(and_4_out), .Cin(1'b0), .S(out_3[2]), .Cout(soma_1bit_2_cout));
  Soma_1bit soma_1bit_3 (.A(soma_1bit_2_cout), .B(and_5_out), .Cin(1'b0), .S(out_3[3]), .Cout(soma_1bit_3_cout));
  Soma_1bit soma_1bit_4 (.A(soma_1bit_3_cout), .B(and_6_out), .Cin(1'b0), .S(out_3[4]), .Cout(soma_1bit_4_cout));
  Soma_1bit soma_1bit_5 (.A(soma_1bit_4_cout), .B(and_7_out), .Cin(1'b0), .S(out_3[5]), .Cout(soma_1bit_5_cout));
  Soma_1bit soma_1bit_6 (.A(soma_1bit_5_cout), .B(and_8_out), .Cin(1'b0), .S(out_3[6]), .Cout(soma_1bit_6_cout));
  Soma_1bit soma_1bit_7 (.A(soma_1bit_6_cout), .B(and_9_out), .Cin(1'b0), .S(out_3[7]), .Cout(soma_1bit_7_cout));
  Soma_1bit soma_1bit_8 (.A(soma_1bit_7_cout), .B(and_10_out), .Cin(1'b0), .S(out_3[8]), .Cout(soma_1bit_8_cout));
  Soma_1bit soma_1bit_9 (.A(soma_1bit_8_cout), .B(and_11_out), .Cin(1'b0), .S(out_3[9]), .Cout(soma_1bit_9_cout));
  Soma_1bit soma_1bit_10 (.A(soma_1bit_9_cout), .B(and_12_out), .Cin(1'b0), .S(out_3[10]), .Cout(soma_1bit_10_cout));
  Soma_1bit soma_1bit_11 (.A(soma_1bit_10_cout), .B(and_13_out), .Cin(1'b0), .S(out_3[11]), .Cout(soma_1bit_11_cout));
  Soma_1bit soma_1bit_12 (.A(soma_1bit_11_cout), .B(and_14_out), .Cin(1'b0), .S(out_3[12]), .Cout(soma_1bit_12_cout));
  Soma_1bit soma_1bit_13 (.A(soma_1bit_12_cout), .B(and_15_out), .Cin(1'b0), .S(out_3[13]), .Cout(soma_1bit_13_cout));
  Soma_1bit soma_1bit_14 (.A(soma_1bit_13_cout), .B(and_16_out), .Cin(1'b0), .S(out_3[14]), .Cout(out_3[15]));

  // Other names for the same wires on the sheet: A1 = A[0]; A2 = A[1]; A3 = A[2]; A4 = A[3]; B1 = B[0]; B2 = B[1];
  //   B3 = B[2]; B4 = B[3]

  // Notes on the sheet:
  //   A: default 1
  //   B: default 1
endmodule
