// Digital circuit Multiplicador-8bit.dig as structural Verilog
module Multiplicador_8bit (
  input  [7:0] A,
  input  [7:0] B,
  output [15:0] out_3,
  output out_4
);

  wire left_shift_3_p1, left_shift_5_p1, left_shift_6_p1, left_shift_8_p1, left_shift_9_p1, left_shift_10_p1,
       left_shift_12_p1, left_shift_13_p1, left_shift_14_p1, left_shift_15_p1, left_shift_17_p1,
       left_shift_18_p1, left_shift_19_p1, left_shift_20_p1, left_shift_21_p1, left_shift_23_p1,
       left_shift_24_p1, left_shift_25_p1, left_shift_26_p1, left_shift_27_p1, left_shift_28_p1,
       soma_16bit_1_cout, soma_16bit_2_cout, soma_16bit_3_cout, soma_16bit_4_cout, soma_16bit_5_cout,
       soma_16bit_6_cout;
  wire [7:0] and_9_out, and_17_out, and_25_out, and_33_out, and_41_out, and_49_out, and_57_out, M1;
  wire [15:0] M2, M3, M4, M5, M6, M7, M8, soma_16bit_1_s, soma_16bit_2_s, soma_16bit_3_s, soma_16bit_4_s,
       soma_16bit_5_s, soma_16bit_6_s;

  and and_1 (M1[0], A[0], B[0]);
  and and_2 (M1[1], A[1], B[0]);
  and and_3 (M1[2], A[2], B[0]);
  and and_4 (M1[3], A[3], B[0]);
  and and_5 (M1[4], A[4], B[0]);
  and and_6 (M1[5], A[5], B[0]);
  and and_7 (M1[6], A[6], B[0]);
  and and_8 (M1[7], A[7], B[0]);
  Soma_16bit soma_16bit_1 (.A({{8{1'b0}}, M1}), .B(M2), .Cin(1'b0), .S(soma_16bit_1_s), .Cout(soma_16bit_1_cout));
  Soma_16bit soma_16bit_2 (
    .A(soma_16bit_1_s), .B(M3), .Cin(soma_16bit_1_cout), .S(soma_16bit_2_s), .Cout(soma_16bit_2_cout));
  Soma_16bit soma_16bit_3 (
    .A(soma_16bit_2_s), .B(M4), .Cin(soma_16bit_2_cout), .S(soma_16bit_3_s), .Cout(soma_16bit_3_cout));
  and and_9 (and_9_out[0], A[0], B[1]);
  and and_10 (and_9_out[1], A[1], B[1]);
  and and_11 (and_9_out[2], A[2], B[1]);
  and and_12 (and_9_out[3], A[3], B[1]);
  and and_13 (and_9_out[4], A[4], B[1]);
  and and_14 (and_9_out[5], A[5], B[1]);
  and and_15 (and_9_out[6], A[6], B[1]);
  and and_16 (and_9_out[7], A[7], B[1]);
  Soma_16bit soma_16bit_4 (
    .A(soma_16bit_3_s), .B(M5), .Cin(soma_16bit_3_cout), .S(soma_16bit_4_s), .Cout(soma_16bit_4_cout));
  Soma_16bit soma_16bit_5 (
    .A(soma_16bit_4_s), .B(M6), .Cin(soma_16bit_4_cout), .S(soma_16bit_5_s), .Cout(soma_16bit_5_cout));
  Soma_16bit soma_16bit_6 (
    .A(soma_16bit_5_s), .B(M7), .Cin(soma_16bit_5_cout), .S(soma_16bit_6_s), .Cout(soma_16bit_6_cout));
  // Left_Shift left_shift_1: pin names not known; wires that end beside it: {{8{1'b0}}, and_9_out}, M2
  Soma_16bit soma_16bit_7 (.A(soma_16bit_6_s), .B(M8), .Cin(soma_16bit_6_cout), .S(out_3), .Cout(out_4));
  and and_17 (and_17_out[0], A[0], B[2]);
  and and_18 (and_17_out[1], A[1], B[2]);
  and and_19 (and_17_out[2], A[2], B[2]);
  and and_20 (and_17_out[3], A[3], B[2]);
  and and_21 (and_17_out[4], A[4], B[2]);
  and and_22 (and_17_out[5], A[5], B[2]);
  and and_23 (and_17_out[6], A[6], B[2]);
  and and_24 (and_17_out[7], A[7], B[2]);
  // Left_Shift left_shift_2: pin names not known; wires that end beside it: {{8{1'b0}}, and_17_out}
  // Left_Shift left_shift_3: pin names not known; wires that end beside it: left_shift_3_p1, left_shift_3_p1, M3
  and and_25 (and_25_out[0], A[0], B[3]);
  and and_26 (and_25_out[1], A[1], B[3]);
  and and_27 (and_25_out[2], A[2], B[3]);
  and and_28 (and_25_out[3], A[3], B[3]);
  and and_29 (and_25_out[4], A[4], B[3]);
  and and_30 (and_25_out[5], A[5], B[3]);
  and and_31 (and_25_out[6], A[6], B[3]);
  and and_32 (and_25_out[7], A[7], B[3]);
  // Left_Shift left_shift_4: pin names not known; wires that end beside it: {{8{1'b0}}, and_25_out}
  // Left_Shift left_shift_5: pin names not known; wires that end beside it: left_shift_5_p1, left_shift_5_p1
  // Left_Shift left_shift_6: pin names not known; wires that end beside it: left_shift_6_p1, left_shift_6_p1, M4
  and and_33 (and_33_out[0], A[0], B[4]);
  and and_34 (and_33_out[1], A[1], B[4]);
  and and_35 (and_33_out[2], A[2], B[4]);
  and and_36 (and_33_out[3], A[3], B[4]);
  and and_37 (and_33_out[4], A[4], B[4]);
  and and_38 (and_33_out[5], A[5], B[4]);
  and and_39 (and_33_out[6], A[6], B[4]);
  and and_40 (and_33_out[7], A[7], B[4]);
  // Left_Shift left_shift_7: pin names not known; wires that end beside it: {{8{1'b0}}, and_33_out}
  // Left_Shift left_shift_8: pin names not known; wires that end beside it: left_shift_8_p1, left_shift_8_p1
  // Left_Shift left_shift_9: pin names not known; wires that end beside it: left_shift_9_p1, left_shift_9_p1
  // Left_Shift left_shift_10: pin names not known; wires that end beside it: left_shift_10_p1, left_shift_10_p1, M5
  and and_41 (and_41_out[0], A[0], B[5]);
  and and_42 (and_41_out[1], A[1], B[5]);
  and and_43 (and_41_out[2], A[2], B[5]);
  and and_44 (and_41_out[3], A[3], B[5]);
  and and_45 (and_41_out[4], A[4], B[5]);
  and and_46 (and_41_out[5], A[5], B[5]);
  and and_47 (and_41_out[6], A[6], B[5]);
  and and_48 (and_41_out[7], A[7], B[5]);
  // Left_Shift left_shift_11: pin names not known; wires that end beside it: {{8{1'b0}}, and_41_out}
  // Left_Shift left_shift_12: pin names not known; wires that end beside it: left_shift_12_p1, left_shift_12_p1
  // Left_Shift left_shift_13: pin names not known; wires that end beside it: left_shift_13_p1, left_shift_13_p1
  // Left_Shift left_shift_14: pin names not known; wires that end beside it: left_shift_14_p1, left_shift_14_p1
  // Left_Shift left_shift_15: pin names not known; wires that end beside it: left_shift_15_p1, left_shift_15_p1, M6
  and and_49 (and_49_out[0], A[0], B[6]);
  and and_50 (and_49_out[1], A[1], B[6]);
  and and_51 (and_49_out[2], A[2], B[6]);
  and and_52 (and_49_out[3], A[3], B[6]);
  and and_53 (and_49_out[4], A[4], B[6]);
  and and_54 (and_49_out[5], A[5], B[6]);
  and and_55 (and_49_out[6], A[6], B[6]);
  and and_56 (and_49_out[7], A[7], B[6]);
  // Left_Shift left_shift_16: pin names not known; wires that end beside it: {{8{1'b0}}, and_49_out}
  // Left_Shift left_shift_17: pin names not known; wires that end beside it: left_shift_17_p1, left_shift_17_p1
  // Left_Shift left_shift_18: pin names not known; wires that end beside it: left_shift_18_p1, left_shift_18_p1
  // Left_Shift left_shift_19: pin names not known; wires that end beside it: left_shift_19_p1, left_shift_19_p1
  // Left_Shift left_shift_20: pin names not known; wires that end beside it: left_shift_20_p1, left_shift_20_p1
  // Left_Shift left_shift_21: pin names not known; wires that end beside it: left_shift_21_p1, left_shift_21_p1, M7
  and and_57 (and_57_out[0], A[0], B[7]);
  and and_58 (and_57_out[1], A[1], B[7]);
  and and_59 (and_57_out[2], A[2], B[7]);
  and and_60 (and_57_out[3], A[3], B[7]);
  and and_61 (and_57_out[4], A[4], B[7]);
  and and_62 (and_57_out[5], A[5], B[7]);
  and and_63 (and_57_out[6], A[6], B[7]);
  and and_64 (and_57_out[7], A[7], B[7]);
  // Left_Shift left_shift_22: pin names not known; wires that end beside it: {{8{1'b0}}, and_57_out}
  // Left_Shift left_shift_23: pin names not known; wires that end beside it: left_shift_23_p1, left_shift_23_p1
  // Left_Shift left_shift_24: pin names not known; wires that end beside it: left_shift_24_p1, left_shift_24_p1
  // Left_Shift left_shift_25: pin names not known; wires that end beside it: left_shift_25_p1, left_shift_25_p1
  // Left_Shift left_shift_26: pin names not known; wires that end beside it: left_shift_26_p1, left_shift_26_p1
  // Left_Shift left_shift_27: pin names not known; wires that end beside it: left_shift_27_p1, left_shift_27_p1
  // Left_Shift left_shift_28: pin names not known; wires that end beside it: left_shift_28_p1, left_shift_28_p1, M8

  // Other names for the same wires on the sheet: A1 = A[0]; A2 = A[1]; A3 = A[2]; A4 = A[3]; A5 = A[4]; A6 = A[5];
  //   A7 = A[6]; A8 = A[7]; B1 = B[0]; B2 = B[1]; B3 = B[2]; B4 = B[3]; B5 = B[4]; B6 = B[5]; B7 = B[6]; B8 = B[7];
  //   Cout = out_4; S[15:0] = out_3
endmodule
