// Digital circuit NAND_8bit.dig as structural Verilog
module NAND_8bit (
  input  [7:0] A,
  input  [7:0] B,
  output [7:0] S
);

  wire [7:0] and_1_out;

  assign and_1_out = A & B;  // And and_1, 8 bits wide
  assign S = ~and_1_out;  // Not not_1, 8 bits wide
endmodule
