// Digital circuit Soma_16bit.dig as structural Verilog
module Soma_16bit (
  input  [15:0] A,
  input  [15:0] B,
  input  Cin,
  output [15:0] S,
  output Cout
);

  wire soma_8bit_1_cout;

  Soma_8bit soma_8bit_1 (.A(A[7:0]), .B(B[7:0]), .Cin(Cin), .Cout(soma_8bit_1_cout), .S(S[7:0]));
  Soma_8bit soma_8bit_2 (.A(A[15:8]), .B(B[15:8]), .Cin(soma_8bit_1_cout), .Cout(Cout), .S(S[15:8]));

  // Other names for the same wires on the sheet: A0[7:0] = A[7:0]; A1[7:0] = A[15:8]; B0[7:0] = B[7:0];
  //   B1[7:0] = B[15:8]; S0[7:0] = S[7:0]; S1[7:0] = S[15:8]
endmodule
