// Digital circuit Soma_4bit.dig as structural Verilog
module Soma_4bit (
  input  [3:0] A,
  input  Cin,
  input  [3:0] B,
  output [3:0] S,
  output Cout
);

  wire soma_1bit_1_cout, soma_1bit_2_cout, soma_1bit_3_cout;

  Soma_1bit soma_1bit_1 (.A(A[0]), .B(B[0]), .Cin(Cin), .S(S[0]), .Cout(soma_1bit_1_cout));
  Soma_1bit soma_1bit_2 (.A(A[1]), .B(B[1]), .Cin(soma_1bit_1_cout), .S(S[1]), .Cout(soma_1bit_2_cout));
  Soma_1bit soma_1bit_3 (.A(A[2]), .B(B[2]), .Cin(soma_1bit_2_cout), .S(S[2]), .Cout(soma_1bit_3_cout));
  Soma_1bit soma_1bit_4 (.A(A[3]), .B(B[3]), .Cin(soma_1bit_3_cout), .S(S[3]), .Cout(Cout));

  // Other names for the same wires on the sheet: A1 = A[0]; A2 = A[1]; A3 = A[2]; A4 = A[3]; B1 = B[0]; B2 = B[1];
  //   B3 = B[2]; B4 = B[3]
endmodule
