// Digital circuit Soma_8bit.dig as structural Verilog
module Soma_8bit (
  input  [7:0] A,
  input  [7:0] B,
  input  Cin,
  output Cout,
  output [7:0] S
);

  wire soma_4bit_1_cout;

  Soma_4bit soma_4bit_1 (.A(A[3:0]), .Cin(Cin), .B(B[3:0]), .S(S[3:0]), .Cout(soma_4bit_1_cout));
  Soma_4bit soma_4bit_2 (.A(A[7:4]), .Cin(soma_4bit_1_cout), .B(B[7:4]), .S(S[7:4]), .Cout(Cout));

  // Other names for the same wires on the sheet: A1[3:0] = A[3:0]; A2[3:0] = A[7:4]; B1[3:0] = B[3:0];
  //   B2[3:0] = B[7:4]
endmodule
