// Digital circuit Subtracao_8bit.dig as structural Verilog
module Subtracao_8bit (
  input  [7:0] A,
  input  [7:0] B,
  input  Cin,
  output Cout,
  output [7:0] S
);

  wire subtracao_4bit_1_cout;

  Subtracao_4bit subtracao_4bit_1 (.A(A[3:0]), .Cin(Cin), .B(B[3:0]), .S(S[3:0]), .Cout(subtracao_4bit_1_cout));
  Subtracao_4bit subtracao_4bit_2 (.A(A[7:4]), .Cin(subtracao_4bit_1_cout), .B(B[7:4]), .S(S[7:4]), .Cout(Cout));

  // Other names for the same wires on the sheet: A1[3:0] = A[3:0]; A2[3:0] = A[7:4]; B1[3:0] = B[3:0];
  //   B2[3:0] = B[7:4]
endmodule
